# Fritzing sketch sbconsole_wiring (saved by Fritzing 0.9.9b)
stripboards: 1

parts:
  MCU1 = Raspberry Pi Zero
  OLED2 = OLED 128x64 I2C Monochrome Display
  U1 = LIPO-1000mAh [package=lipo-1000]
  SparkFun_LiPo_Charger_Booster-5V1A1 = SparkFun LiPo Charger Booster-5V1A [part_number="PRT-14411 "]
  S3 = Pushbutton [package="[THT]"]
  S4 = Pushbutton [package="[THT]"]
  S5 = Pushbutton [package="[THT]"]
  S6 = Pushbutton [package="[THT]"]
  S7 = Pushbutton [package="[THT]"]
  S8 = Pushbutton [package="[THT]"]

nets:
  N1: MCU1.pin_1, OLED2.VDD
  N2: MCU1.pin_2, SparkFun_LiPo_Charger_Booster-5V1A1.VCC
  N3: MCU1.pin_3, OLED2.SDA
  N4: MCU1.pin_5, OLED2.SCK
  GND: MCU1.pin_6, MCU1.pin_9, OLED2.GND, U1.-, SparkFun_LiPo_Charger_Booster-5V1A1.GND, S3.Pin_3, S3.Pin_4, S4.Pin_3, S4.Pin_4, S5.Pin_3, S5.Pin_4, S6.Pin_3, S6.Pin_4, S7.Pin_3, S7.Pin_4, S8.Pin_3, S8.Pin_4
  N5: MCU1.pin_33, S8.Pin_1, S8.Pin_2
  N6: MCU1.pin_35, S7.Pin_1, S7.Pin_2
  N7: MCU1.pin_36, S6.Pin_1, S6.Pin_2
  N8: MCU1.pin_37, S5.Pin_1, S5.Pin_2
  N9: MCU1.pin_38, S4.Pin_1, S4.Pin_2
  N10: MCU1.pin_40, S3.Pin_1, S3.Pin_2
  N11: U1.+, SparkFun_LiPo_Charger_Booster-5V1A1.1

custom parts:
  SparkFun LiPo Charger Booster-5V1A: The SparkFun 5V/1A LiPo Charger/Booster is a no-nonsense circuit for generating one amp from a Lithium Polymer battery at 5V. This LiPo charger is a very economical choice that is equipped with a simple booster circuit utilizing the PAM2401 IC, and includes protection diodes so you can run multiple cells in series for an extra kick. While the booster circuit is in operation, this board can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
